// Logisim project logism_design.circ as structural Verilog: 8 circuits, main circuit processor
module processor (
  input  [17:0] in_1
);

  wire ADD;

  Decoder #(.select(4), .enable("false")) decoder_1 (
    .out0(ADD), .sel(in_1[3:0]));  // open: out1, out2, out3, out4, out5, out6, out7, out8, out9, out10, out11, out12, out13, out14, out15
  _16_bit_adder u_16_bit_adder_1 ();  // open: in_1, in_2, in_3, out_4, out_5

  // Other names for the same wires on the sheet: ADDR[9:0] = in_1[13:4]; REG0[3:0] = in_1[7:4];
  //   REG1[3:0] = in_1[11:8]; IMM[5:0] = in_1[17:12]; REG2[3:0] = in_1[15:12]

  // Notes on the sheet:
  //   ASSEMBLY CODE
  //   OP CODE
  //   MEM INPUT
endmodule

module half_adder (
  input  A,
  input  B,
  output out_3,
  output out_4
);

  xor xor_1 (out_3, A, B);
  and and_1 (out_4, A, B);
endmodule

module full_adder (
  input  in_1,
  input  in_2,
  input  in_3,
  output out_4,
  output out_5
);

  wire and_1_out, and_2_out, xor_1_out;

  xor xor_1 (xor_1_out, in_1, in_2);
  xor xor_2 (out_4, xor_1_out, in_3);
  and and_1 (and_1_out, xor_1_out, in_3);
  and and_2 (and_2_out, in_2, in_1);
  or or_1 (out_5, and_1_out, and_2_out);
endmodule

module _2_bit_adder (
  input  [1:0] A,
  input  [1:0] B,
  input  C,
  output [1:0] sum,
  output out_5
);

  wire full_adder_1_out_5;

  full_adder full_adder_1 (.in_1(A[0]), .in_2(B[0]), .in_3(C), .out_4(sum[0]), .out_5(full_adder_1_out_5));
  full_adder full_adder_2 (.in_1(A[1]), .in_2(B[1]), .in_3(full_adder_1_out_5), .out_4(sum[1]), .out_5(out_5));
endmodule

module _4_bit_adder (
  input  [3:0] A,
  input  [3:0] B,
  input  C,
  output out_4,
  output [3:0] out_5
);

  wire n2_bit_adder_1_out_5;

  _2_bit_adder u_2_bit_adder_1 (.A(A[1:0]), .B(B[1:0]), .C(C), .out_5(n2_bit_adder_1_out_5), .sum(out_5[1:0]));
  _2_bit_adder u_2_bit_adder_2 (.A(A[3:2]), .B(B[3:2]), .C(n2_bit_adder_1_out_5), .out_5(out_4), .sum(out_5[3:2]));
endmodule

module _8_bit_adder (
  input  [7:0] in_1,
  input  [7:0] in_2,
  input  in_3,
  output out_4,
  output [7:0] out_5
);

  wire n4_bit_adder_1_out_4;

  _4_bit_adder u_4_bit_adder_1 (
    .A(in_1[3:0]), .B(in_2[3:0]), .C(in_3), .out_4(n4_bit_adder_1_out_4), .out_5(out_5[3:0]));
  _4_bit_adder u_4_bit_adder_2 (
    .A(in_1[7:4]), .B(in_2[7:4]), .C(n4_bit_adder_1_out_4), .out_4(out_4), .out_5(out_5[7:4]));
endmodule

module _16_bit_adder (
  input  [15:0] in_1,
  input  [15:0] in_2,
  input  in_3,
  output out_4,
  output [15:0] out_5
);

  wire n8_bit_adder_1_out_4;

  _8_bit_adder u_8_bit_adder_1 (
    .in_1(in_1[7:0]), .in_2(in_2[7:0]), .in_3(in_3), .out_4(n8_bit_adder_1_out_4), .out_5(out_5[7:0]));
  _8_bit_adder u_8_bit_adder_2 (
    .in_1(in_1[15:8]), .in_2(in_2[15:8]), .in_3(n8_bit_adder_1_out_4), .out_4(out_4), .out_5(out_5[15:8]));
endmodule

module ALU (
);


  // Notes on the sheet:
  //   ADD
  //   AND
  //   NAND
  //   XOR
endmodule
